// Logisim project 74Logic.circ as structural Verilog: 8 circuits, main circuit SN74LS01
module SN74LS01 (
  input  A1,
  input  B1,
  input  A2,
  input  B2,
  input  A3,
  input  B3,
  input  A4,
  input  B4,
  output Y1,
  output Y2,
  output Y3,
  output Y4
);

  wire and_1_out, and_2_out, and_3_out, and_4_out;

  and and_1 (and_1_out, A1, B1);
  and and_2 (and_2_out, A2, B2);
  and and_3 (and_3_out, A3, B3);
  and and_4 (and_4_out, A4, B4);
  assign Y1 = and_1_out ? 1'b0 : 1'bz;  // Controlled_Buffer controlled_buffer_1
  assign Y2 = and_2_out ? 1'b0 : 1'bz;  // Controlled_Buffer controlled_buffer_2
  assign Y3 = and_3_out ? 1'b0 : 1'bz;  // Controlled_Buffer controlled_buffer_3
  assign Y4 = and_4_out ? 1'b0 : 1'bz;  // Controlled_Buffer controlled_buffer_4
endmodule

module SN74LS03 (
  input  A1,
  input  B1,
  input  A2,
  input  B2,
  input  A3,
  input  B3,
  input  A4,
  input  B4,
  output Y1,
  output Y2,
  output Y3,
  output Y4
);

  wire and_1_out, and_2_out, and_3_out, and_4_out;

  and and_1 (and_1_out, A1, B1);
  and and_2 (and_2_out, A2, B2);
  and and_3 (and_3_out, A3, B3);
  and and_4 (and_4_out, A4, B4);
  assign Y1 = and_1_out ? 1'b0 : 1'bz;  // Controlled_Buffer controlled_buffer_1
  assign Y2 = and_2_out ? 1'b0 : 1'bz;  // Controlled_Buffer controlled_buffer_2
  assign Y3 = and_3_out ? 1'b0 : 1'bz;  // Controlled_Buffer controlled_buffer_3
  assign Y4 = and_4_out ? 1'b0 : 1'bz;  // Controlled_Buffer controlled_buffer_4
endmodule

module SN74LS05 (
  input  A1,
  input  A2,
  input  A3,
  input  A4,
  input  A5,
  input  A6,
  output Y1,
  output Y2,
  output Y3,
  output Y4,
  output Y5,
  output Y6
);

  assign Y1 = A1 ? 1'b0 : 1'bz;  // Controlled_Buffer controlled_buffer_1
  assign Y2 = A2 ? 1'b0 : 1'bz;  // Controlled_Buffer controlled_buffer_2
  assign Y3 = A3 ? 1'b0 : 1'bz;  // Controlled_Buffer controlled_buffer_3
  assign Y4 = A4 ? 1'b0 : 1'bz;  // Controlled_Buffer controlled_buffer_4
  assign Y5 = A5 ? 1'b0 : 1'bz;  // Controlled_Buffer controlled_buffer_5
  assign Y6 = A6 ? 1'b0 : 1'bz;  // Controlled_Buffer controlled_buffer_6
endmodule

module SN74LS06 (
  input  A1,
  input  A2,
  input  A3,
  input  A4,
  input  A5,
  input  A6,
  output Y1,
  output Y2,
  output Y3,
  output Y4,
  output Y5,
  output Y6
);

  assign Y1 = A1 ? 1'b0 : 1'bz;  // Controlled_Buffer controlled_buffer_1
  assign Y2 = A2 ? 1'b0 : 1'bz;  // Controlled_Buffer controlled_buffer_2
  assign Y3 = A3 ? 1'b0 : 1'bz;  // Controlled_Buffer controlled_buffer_3
  assign Y4 = A4 ? 1'b0 : 1'bz;  // Controlled_Buffer controlled_buffer_4
  assign Y5 = A5 ? 1'b0 : 1'bz;  // Controlled_Buffer controlled_buffer_5
  assign Y6 = A6 ? 1'b0 : 1'bz;  // Controlled_Buffer controlled_buffer_6
endmodule

module SN74LS07 (
  input  A1,
  input  A2,
  input  A3,
  input  A4,
  input  A5,
  input  A6,
  output Y1,
  output Y2,
  output Y3,
  output Y4,
  output Y5,
  output Y6
);

  wire not_1_out, not_2_out, not_3_out, not_4_out, not_5_out, not_6_out;

  assign Y1 = not_1_out ? 1'b0 : 1'bz;  // Controlled_Buffer controlled_buffer_1
  not not_1 (not_1_out, A1);
  assign Y2 = not_2_out ? 1'b0 : 1'bz;  // Controlled_Buffer controlled_buffer_2
  not not_2 (not_2_out, A2);
  assign Y3 = not_3_out ? 1'b0 : 1'bz;  // Controlled_Buffer controlled_buffer_3
  not not_3 (not_3_out, A3);
  assign Y4 = not_4_out ? 1'b0 : 1'bz;  // Controlled_Buffer controlled_buffer_4
  not not_4 (not_4_out, A4);
  assign Y5 = not_5_out ? 1'b0 : 1'bz;  // Controlled_Buffer controlled_buffer_5
  not not_5 (not_5_out, A5);
  assign Y6 = not_6_out ? 1'b0 : 1'bz;  // Controlled_Buffer controlled_buffer_6
  not not_6 (not_6_out, A6);
endmodule

module SN74LS09 (
  input  A1,
  input  B1,
  input  A2,
  input  B2,
  input  A3,
  input  B3,
  input  A4,
  input  B4,
  output Y1,
  output Y2,
  output Y3,
  output Y4
);

  wire nand_1_out, nand_2_out, nand_3_out, nand_4_out;

  nand nand_1 (nand_1_out, A1, B1);
  nand nand_2 (nand_2_out, A2, B2);
  nand nand_3 (nand_3_out, A3, B3);
  nand nand_4 (nand_4_out, A4, B4);
  assign Y1 = nand_1_out ? 1'b0 : 1'bz;  // Controlled_Buffer controlled_buffer_1
  assign Y2 = nand_2_out ? 1'b0 : 1'bz;  // Controlled_Buffer controlled_buffer_2
  assign Y3 = nand_3_out ? 1'b0 : 1'bz;  // Controlled_Buffer controlled_buffer_3
  assign Y4 = nand_4_out ? 1'b0 : 1'bz;  // Controlled_Buffer controlled_buffer_4
endmodule

module SN74LS12 (
  input  A1,
  input  B1,
  input  C1,
  input  A2,
  input  B2,
  input  C2,
  input  A3,
  input  B3,
  input  C3,
  output Y1,
  output Y2,
  output Y3
);

  wire and_1_out, and_2_out, and_3_out;

  and and_1 (and_1_out, A1, B1, C1);
  and and_2 (and_2_out, A2, B2, C2);
  and and_3 (and_3_out, A3, B3, C3);
  assign Y1 = and_1_out ? 1'b0 : 1'bz;  // Controlled_Buffer controlled_buffer_1
  assign Y2 = and_2_out ? 1'b0 : 1'bz;  // Controlled_Buffer controlled_buffer_2
  assign Y3 = and_3_out ? 1'b0 : 1'bz;  // Controlled_Buffer controlled_buffer_3
endmodule

module SN74LS38 (
  input  A1,
  input  B1,
  input  A2,
  input  B2,
  input  A3,
  input  B3,
  input  A4,
  input  B4,
  output Y1,
  output Y2,
  output Y3,
  output Y4
);

  wire and_1_out, and_2_out, and_3_out, and_4_out;

  and and_1 (and_1_out, A1, B1);
  and and_2 (and_2_out, A2, B2);
  and and_3 (and_3_out, A3, B3);
  and and_4 (and_4_out, A4, B4);
  assign Y1 = and_1_out ? 1'b0 : 1'bz;  // Controlled_Buffer controlled_buffer_1
  assign Y2 = and_2_out ? 1'b0 : 1'bz;  // Controlled_Buffer controlled_buffer_2
  assign Y3 = and_3_out ? 1'b0 : 1'bz;  // Controlled_Buffer controlled_buffer_3
  assign Y4 = and_4_out ? 1'b0 : 1'bz;  // Controlled_Buffer controlled_buffer_4
endmodule
